// Digital circuit 32_bit_ALU.dig as structural Verilog
module _32_bit_ALU (
  input  [31:0] A,
  input  [31:0] B,
  input  [1:0] C,
  output [31:0] R,
  output ZF,
  output CF
);

  wire add_1_c_o, sub_1_c_o;
  wire [31:0] add_1_s, and_1_out, or_1_out, sub_1_s;

  assign and_1_out = A & B;  // And and_1, 32 bits wide
  assign or_1_out = A | B;  // Or or_1, 32 bits wide
  Add #(.Bits(32)) add_1 (.a(A), .b(B), .c_i(1'b0), .s(add_1_s), .c_o(add_1_c_o));
  Sub #(.Bits(32)) sub_1 (.a(A), .b(B), .c_i(1'b0), .s(sub_1_s), .c_o(sub_1_c_o));
  Multiplexer #(.Selector_Bits(2), .Bits(32)) multiplexer_1 (
    .sel(C), .in_0(and_1_out), .in_1(or_1_out), .in_2(add_1_s), .in_3(sub_1_s), .out(R));
  _32_bit_Zero_Flag _32_bit_zero_flag_1 (.IN(R), .ZF(ZF));
  or or_2 (CF, add_1_c_o, sub_1_c_o);
endmodule
