// Digital circuit 32_bit_AddSub.dig as structural Verilog
module _32_bit_AddSub (
  input  [31:0] A,
  input  [31:0] B,
  input  [1:0] C,
  output CF,
  output [31:0] S,
  output OF,
  output S0,
  output S_2,
  output S_3,
  output S_4,
  output S_5,
  output S_6,
  output S_7,
  output S_8,
  output S_9,
  output S_10,
  output S_11,
  output S_12,
  output S_13,
  output S_14,
  output S_15,
  output S_16,
  output S_17,
  output S_18,
  output S_19,
  output S_20,
  output S_21,
  output S_22,
  output S_23,
  output S_24,
  output S_25,
  output S_26,
  output S_27,
  output S_28,
  output S_29,
  output S_30,
  output S_31,
  output S_32
);

  wire _4_bit_bitwiseadder_1_c4, _4_bit_bitwiseadder_2_c4, _4_bit_bitwiseadder_3_c4,
       _4_bit_bitwiseadder_4_c4, _4_bit_bitwiseadder_5_c4, _4_bit_bitwiseadder_6_c4,
       _4_bit_bitwiseadder_7_c4, _4_bit_bitwiseadder_8_c3, not_1_out;
  wire [3:0] xor_1_out_2, xor_1_out_3;
  wire [31:0] xor_1_out;
  wire [31:31] and_1_out;

  not not_1 (not_1_out, C[0]);
  and and_1 (and_1_out[31], not_1_out, C[1]);
  assign {xor_1_out[31:12], xor_1_out_3, xor_1_out_2, xor_1_out[3:0]} = B ^ {32{and_1_out[31]}};  // XOr xor_1, 32 bits wide
  _4_bit_BitWiseAdder _4_bit_bitwiseadder_1 (
    .A(A[3:0]), .B(xor_1_out[3:0]), .C0(1'b0), .C4(_4_bit_bitwiseadder_1_c4), .S(S[3:0]));  // open: C3
  _4_bit_BitWiseAdder _4_bit_bitwiseadder_2 (
    .A(A[7:4]), .B(xor_1_out_2), .C0(_4_bit_bitwiseadder_1_c4), .C4(_4_bit_bitwiseadder_2_c4), .S(S[7:4]));  // open: C3
  _4_bit_BitWiseAdder _4_bit_bitwiseadder_3 (
    .A(A[11:8]), .B(xor_1_out_3), .C0(_4_bit_bitwiseadder_2_c4), .C4(_4_bit_bitwiseadder_3_c4), .S(S[11:8]));  // open: C3
  _4_bit_BitWiseAdder _4_bit_bitwiseadder_4 (
    .A(A[15:12]), .B(xor_1_out[15:12]), .C0(_4_bit_bitwiseadder_3_c4), .C4(_4_bit_bitwiseadder_4_c4),
    .S(S[15:12]));  // open: C3
  _4_bit_BitWiseAdder _4_bit_bitwiseadder_5 (
    .A(A[19:16]), .B(xor_1_out[19:16]), .C0(_4_bit_bitwiseadder_4_c4), .C4(_4_bit_bitwiseadder_5_c4),
    .S(S[19:16]));  // open: C3
  _4_bit_BitWiseAdder _4_bit_bitwiseadder_6 (
    .A(A[23:20]), .B(xor_1_out[23:20]), .C0(_4_bit_bitwiseadder_5_c4), .C4(_4_bit_bitwiseadder_6_c4),
    .S(S[23:20]));  // open: C3
  _4_bit_BitWiseAdder _4_bit_bitwiseadder_7 (
    .A(A[27:24]), .B(xor_1_out[27:24]), .C0(_4_bit_bitwiseadder_6_c4), .C4(_4_bit_bitwiseadder_7_c4),
    .S(S[27:24]));  // open: C3
  _4_bit_BitWiseAdder _4_bit_bitwiseadder_8 (
    .A(A[31:28]), .B(xor_1_out[31:28]), .C0(_4_bit_bitwiseadder_7_c4), .C4(CF),
    .C3(_4_bit_bitwiseadder_8_c3), .S(S[31:28]));
  xor xor_2 (OF, CF, _4_bit_bitwiseadder_8_c3);

  assign S0 = S[0];
  assign S_2 = S[1];
  assign S_3 = S[2];
  assign S_4 = S[3];
  assign S_5 = S[4];
  assign S_6 = S[5];
  assign S_7 = S[6];
  assign S_8 = S[7];
  assign S_9 = S[8];
  assign S_10 = S[9];
  assign S_11 = S[10];
  assign S_12 = S[11];
  assign S_13 = S[12];
  assign S_14 = S[13];
  assign S_15 = S[14];
  assign S_16 = S[15];
  assign S_17 = S[16];
  assign S_18 = S[17];
  assign S_19 = S[18];
  assign S_20 = S[19];
  assign S_21 = S[20];
  assign S_22 = S[21];
  assign S_23 = S[22];
  assign S_24 = S[23];
  assign S_25 = S[24];
  assign S_26 = S[25];
  assign S_27 = S[26];
  assign S_28 = S[27];
  assign S_29 = S[28];
  assign S_30 = S[29];
  assign S_31 = S[30];
  assign S_32 = S[31];
endmodule
