// Digital circuit 32_bit_Zero_Flag.dig as structural Verilog
module _32_bit_Zero_Flag (
  input  [31:0] IN,
  output ZF
);

  wire or_1_out;

  or or_1 (or_1_out, IN[0], IN[1], IN[2], IN[3], IN[4], IN[5], IN[6], IN[7], IN[8], IN[9], IN[10], IN[11], IN[12], IN[13], IN[14], IN[15], IN[17], IN[18], IN[19], IN[20], IN[21], IN[22], IN[23], IN[24], IN[25], IN[26], IN[27], IN[28], IN[29], IN[30], IN[31], IN[16]);
  not not_1 (ZF, or_1_out);
endmodule
