// Digital circuit 4_bit_BitWiseAdder.dig as structural Verilog
module _4_bit_BitWiseAdder (
  input  [3:0] A,
  input  [3:0] B,
  input  C0,
  output C4,
  output C3,
  output [3:0] S
);

  FourBitAdder fourbitadder_1 (
    .X0(A[0]), .X1(A[1]), .X2(A[2]), .X3(A[3]), .C0(C0), .Y0(B[0]), .Y1(B[1]), .Y2(B[2]), .Y3(B[3]),
    .S0(S[0]), .S1(S[1]), .S2(S[2]), .S3(S[3]), .C4(C4), .C3(C3));
endmodule
