// Digital circuit FourBitAddSub.dig as structural Verilog
module FourBitAddSub (
  input  Y0,
  input  Y1,
  input  Y2,
  input  Y3,
  input  X0,
  input  X1,
  input  X2,
  input  X3,
  input  M,
  output S0,
  output S1,
  output S2,
  output S3,
  output OF,
  output CF
);

  wire fourbitadder_1_c3, fourbitadder_1_c4, xor_3_out, xor_4_out, xor_5_out, xor_6_out;

  xor xor_1 (OF, fourbitadder_1_c4, fourbitadder_1_c3);
  xor xor_2 (CF, fourbitadder_1_c4, M);
  xor xor_3 (xor_3_out, X3, M);
  FourBitAdder fourbitadder_1 (
    .X0(xor_6_out), .X1(xor_5_out), .X2(xor_4_out), .X3(xor_3_out), .C0(M), .Y0(Y0), .Y1(Y1), .Y2(Y2),
    .Y3(Y3), .S0(S0), .S1(S1), .S2(S2), .S3(S3), .C4(fourbitadder_1_c4), .C3(fourbitadder_1_c3));
  xor xor_4 (xor_4_out, X2, M);
  xor xor_5 (xor_5_out, X1, M);
  xor xor_6 (xor_6_out, X0, M);
endmodule
