// Digital circuit FourBitAdder.dig as structural Verilog
module FourBitAdder (
  input  X0,
  input  X1,
  input  X2,
  input  X3,
  input  C0,
  input  Y0,
  input  Y1,
  input  Y2,
  input  Y3,
  output S0,
  output S1,
  output S2,
  output S3,
  output C4,
  output C3
);

  wire fulladder_3_c, fulladder_4_c;

  FullAdder fulladder_1 (.X(C3), .Y(X3), .Z(Y3), .S(S3), .C(C4));
  FullAdder fulladder_2 (.X(fulladder_3_c), .Y(X2), .Z(Y2), .S(S2), .C(C3));
  FullAdder fulladder_3 (.X(fulladder_4_c), .Y(X1), .Z(Y1), .S(S1), .C(fulladder_3_c));
  FullAdder fulladder_4 (.X(C0), .Y(X0), .Z(Y0), .S(S0), .C(fulladder_4_c));
endmodule
