// Digital circuit FullAdder.dig as structural Verilog
module FullAdder (
  input  X,
  input  Y,
  input  Z,
  output S,
  output C
);

  wire halfadder_1_c, halfadder_1_s, halfadder_2_c;

  HalfAdder halfadder_1 (.X(X), .Y(Y), .S(halfadder_1_s), .C(halfadder_1_c));
  HalfAdder halfadder_2 (.X(halfadder_1_s), .Y(Z), .S(S), .C(halfadder_2_c));
  or or_1 (C, halfadder_2_c, halfadder_1_c);
endmodule
